// Logisim project ALU.circ as structural Verilog: 10 circuits, main circuit ALU
module ALU (
  input  OP,
  input  [7:0] A,
  input  [7:0] B,
  output [7:0] R,
  output C,
  output V
);

  wire [7:0] xor_1_out;

  assign xor_1_out = {8{OP}} ^ B;  // XOR_Gate xor_1, 8 bits wide
  Add8bits Add8bits_1 (.C_in(OP), .A(A), .B(xor_1_out), .R(R), .C_out(C));
  overflow overflow_1 (.Input_2(A[7]), .Input_1(xor_1_out[7]), .Input_3(R[7]), .V(V));
endmodule

module Add1bit (
  input  A,
  input  B,
  input  C_in,
  output D,
  output C_out
);

  wire AND_2_out, AND_3_out, AND_out, XOR_out;

  xor XOR (XOR_out, A, B);
  and AND (AND_out, A, B);
  and AND_2 (AND_2_out, A, C_in);
  and AND_3 (AND_3_out, B, C_in);
  xor XOR_2 (D, XOR_out, C_in);
  or OR (C_out, AND_out, AND_2_out, AND_3_out);
endmodule

module Add4bits (
  input  C_in,
  input  [3:0] A,
  input  [3:0] B,
  output [3:0] S,
  output C_out
);

  wire Add1bit_2_c_out, Add1bit_3_c_out, Add1bit_4_c_out;

  Add1bit Add1bit_3 (.A(A[0]), .D(S[0]), .B(B[0]), .C_in(C_in), .C_out(Add1bit_3_c_out));
  Add1bit Add1bit_2 (.A(A[1]), .D(S[1]), .B(B[1]), .C_in(Add1bit_3_c_out), .C_out(Add1bit_2_c_out));
  Add1bit Add1bit_4 (.A(A[2]), .D(S[2]), .B(B[2]), .C_in(Add1bit_2_c_out), .C_out(Add1bit_4_c_out));
  Add1bit Add1bit_1 (.A(A[3]), .D(S[3]), .B(B[3]), .C_in(Add1bit_4_c_out), .C_out(C_out));
endmodule

module Add8bits (
  input  C_in,
  input  [7:0] A,
  input  [7:0] B,
  output [7:0] R,
  output C_out
);

  wire Add4bits_1_c_out;

  Add4bits Add4bits_1 (.C_in(C_in), .A(A[3:0]), .B(B[3:0]), .S(R[3:0]), .C_out(Add4bits_1_c_out));
  Add4bits Add4bits_2 (.C_in(Add4bits_1_c_out), .A(A[7:4]), .B(B[7:4]), .S(R[7:4]), .C_out(C_out));
endmodule

module Sous8bits (
  input  [7:0] A,
  input  [7:0] B,
  output [7:0] out_3
);

  wire add8bits_1_p3;
  wire [7:0] not_1_out;

  assign not_1_out = ~B;  // NOT_Gate not_1, 8 bits wide
  // Add8bits add8bits_1: pin names not known; wires that end beside it: A, not_1_out, add8bits_1_p3
  // Add8bits add8bits_2: pin names not known; wires that end beside it: add8bits_1_p3, 8'h1, out_3
endmodule

module overflow (
  input  Input_2,
  input  Input_1,
  input  Input_3,
  output V
);

  wire and_1_out, and_2_out, not_1_out, not_2_out, not_3_out;

  not not_1 (not_1_out, Input_3);
  not not_2 (not_2_out, Input_2);
  not not_3 (not_3_out, Input_1);
  and and_1 (and_1_out, Input_2, Input_1, not_1_out);
  and and_2 (and_2_out, not_2_out, not_3_out, Input_3);
  or or_1 (V, and_1_out, and_2_out);
endmodule

module ALUComplexe (
  input  [2:0] OP,
  input  [7:0] A,
  input  [7:0] B,
  output Z,
  output N,
  output [7:0] R,
  output C,
  output V
);

  wire A_Shift_Right_c, ALUSimple_c, Shift_Left_c, Shift_Right_c;
  wire [7:0] A_Shift_Right_r, ALUSimple_r, ETbb_out, NON_out, OUbb_out, Shift_Left_r, Shift_Right_r;

  ALU ALUSimple (.OP(OP[0]), .A(A), .B(B), .R(ALUSimple_r), .C(ALUSimple_c), .V(V));
  ShiftLeft Shift_Left (.A(A), .R(Shift_Left_r), .C(Shift_Left_c));
  ShiftRight Shift_Right (.A(A), .C(Shift_Right_c), .R(Shift_Right_r));
  ArithmetiqueShiftRight A_Shift_Right (.A(A), .C(A_Shift_Right_c), .R(A_Shift_Right_r));
  assign ETbb_out = A & B;  // AND_Gate ETbb, 8 bits wide
  assign OUbb_out = A | B;  // OR_Gate OUbb, 8 bits wide
  assign NON_out = ~A;  // NOT_Gate NON, 8 bits wide
  Multiplexer #(.select(3)) multiplexer_1 (
    .in0(ALUSimple_c), .in1(ALUSimple_c), .in2(Shift_Left_c), .in3(Shift_Right_c), .in4(A_Shift_Right_c),
    .in5(1'b0), .in6(1'b0), .in7(1'b0), .out(C), .sel(OP));  // open: en
  Multiplexer #(.select(3), .width(8)) multiplexer_2 (
    .in0(ALUSimple_r), .in1(ALUSimple_r), .in2(Shift_Left_r), .in3(Shift_Right_r), .in4(A_Shift_Right_r),
    .in5(ETbb_out), .in6(OUbb_out), .in7(NON_out), .out({N, R[6:0]}), .sel(OP));  // open: en
  and and_1 (Z, ~R[0], ~R[1], ~R[2], ~R[3], ~R[5], ~R[5], ~R[6], ~N);  // AND_Gate

  assign R[7] = N;
endmodule

module ShiftLeft (
  input  [7:0] A,
  output [7:0] R,
  output C
);


  assign C = A[7];
  assign R = {A[6:0], 1'b0};
endmodule

module ShiftRight (
  input  [7:0] A,
  output C,
  output [7:0] R
);


  assign C = A[0];
  assign R = {1'b0, A[7:1]};
endmodule

module ArithmetiqueShiftRight (
  input  [7:0] A,
  output C,
  output [7:0] R
);


  assign C = A[0];
  assign R = {{2{A[7]}}, A[6:1]};
endmodule
