// Logisim project cpu.circ as structural Verilog: 4 circuits, main circuit cpu
module cpu (
  input  clk,
  input  Reset,
  input  [7:0] DataIn,
  output [7:0] AddrPeriph,
  output [7:0] DataOut,
  output OutEn
);

  wire and_1_out, and_2_out, or_2_out, UCCPU_conditionenable, UCCPU_pcload, UCCPU_writeregister;
  wire [1:0] UCCPU_loadselect;
  wire [2:0] UCCPU_aluop, UCCPU_resultat, UCCPU_source0, UCCPU_source1;
  wire [3:0] ALU_z, or_1_out, register_1_q, UCCPU_condition;
  wire [6:0] counter_1_q, UCCPU_newpc;
  wire [7:0] ALU_r, multiplexer_1_out, Registers_outb;
  wire [15:0] rom_instructions_data_out;

  Counter #(.width(7), .max('h7f)) counter_1 (
    .clr(Reset), .load(and_2_out), .clk(clk), .D(UCCPU_newpc), .Q(counter_1_q));  // open: up, count, carry
  rom rom_instructions (.addr(counter_1_q), .data_out(rom_instructions_data_out));
  UC UCCPU (
    .Instruction(rom_instructions_data_out), .PC(counter_1_q), .PCLoad(UCCPU_pcload), .NewPC(UCCPU_newpc),
    .ConditionEnable(UCCPU_conditionenable), .Condition(UCCPU_condition), .Source0(UCCPU_source0),
    .Source1(UCCPU_source1), .Resultat(UCCPU_resultat), .ALUOP(UCCPU_aluop),
    .WriteRegister(UCCPU_writeregister), .LoadValue(AddrPeriph), .LoadSelect(UCCPU_loadselect),
    .PeriphOutEn(OutEn));
  Multiplexer #(.select(2), .width(8), .enable("false")) multiplexer_1 (
    .in0(ALU_r), .in1(AddrPeriph), .in2(DataIn), .in3(DataIn), .out(multiplexer_1_out), .sel(UCCPU_loadselect));
  memoire Registers (
    .A(UCCPU_source0), .B(UCCPU_source1), .AddressWrite(UCCPU_resultat), .WriteValue(multiplexer_1_out),
    .AllowWrite(UCCPU_writeregister), .Reset(Reset), .clk(clk), .OutA(DataOut), .OutB(Registers_outb));
  ALUComplexe ALU (
    .OP(UCCPU_aluop), .A(DataOut), .B(Registers_outb), .Z(ALU_z[0]), .N(ALU_z[1]), .R(ALU_r), .C(ALU_z[2]),
    .V(ALU_z[3]));
  Register #(.width(4)) register_1 (.D(ALU_z), .en(1'b1), .clk(clk), .Q(register_1_q));  // open: clr
  assign or_1_out = ~UCCPU_condition | register_1_q;  // OR_Gate or_1, 4 bits wide
  and and_1 (and_1_out, or_1_out[0], or_1_out[1], or_1_out[2], or_1_out[3]);
  or or_2 (or_2_out, ~UCCPU_conditionenable, and_1_out);  // OR_Gate
  and and_2 (and_2_out, UCCPU_pcload, or_2_out);
endmodule

module UC (
  input  [15:0] Instruction,
  input  [6:0] PC,
  output PCLoad,
  output [6:0] NewPC,
  output ConditionEnable,
  output [3:0] Condition,
  output [2:0] Source0,
  output [2:0] Source1,
  output [2:0] Resultat,
  output [2:0] ALUOP,
  output WriteRegister,
  output [7:0] LoadValue,
  output [1:0] LoadSelect,
  output PeriphOutEn
);

  wire comparator_1_eq;
  wire [7:0] bit_extender_1_out;
  wire [7:7] adder_1_out;

  Comparator #(.width(4)) comparator_1 (.a(4'b1000), .b(Instruction[15:12]), .eq(comparator_1_eq));  // open: gt, lt
  Comparator #(.width(4)) comparator_2 (.a(4'b1100), .b(Instruction[15:12]), .eq(LoadSelect[1]));  // open: gt, lt
  Comparator #(.width(4)) comparator_3 (.a(4'b1101), .b(Instruction[15:12]), .eq(PeriphOutEn));  // open: gt, lt
  Comparator #(.width(3)) comparator_4 (.a(Instruction[15:13]), .b(3'b101), .eq(PCLoad));  // open: gt, lt
  assign bit_extender_1_out = {{1{PC[6]}}, PC};  // Bit_Extender bit_extender_1
  Adder adder_1 (.a(bit_extender_1_out), .b(Instruction[7:0]), .out({adder_1_out[7], NewPC}));  // open: cin, cout
  not not_1 (ConditionEnable, Instruction[12]);
  Multiplexer #(.width(3), .enable("false")) multiplexer_1 (
    .in0(Instruction[8:6]), .in1(Instruction[11:9]), .out(Source0), .sel(PeriphOutEn));
  or or_1 (WriteRegister, ~Instruction[15], comparator_1_eq, LoadSelect[1]);  // OR_Gate

  assign ALUOP = Instruction[14:12];
  assign Condition = Instruction[11:8];
  assign LoadSelect[0] = Instruction[15];
  assign LoadValue = Instruction[7:0];
  assign Resultat = Instruction[11:9];
  assign Source1 = Instruction[5:3];
endmodule

module CPU_Interface (
  input  clk,
  input  Reset,
  input  [7:0] PeriphWrite1,
  input  PeriphWE1,
  input  [7:0] PeriphWrite2,
  input  PeriphWE2,
  input  [7:0] PeriphWrite3,
  input  PeriphWE3,
  input  [7:0] PeriphWrite4,
  input  PeriphWE4,
  input  [7:0] PeriphWrite5,
  input  PeriphWE5,
  input  [7:0] PeriphWrite6,
  input  PeriphWE6,
  input  [7:0] PeriphWrite7,
  input  PeriphWE7,
  input  [7:0] PeriphWrite8,
  input  PeriphWE8,
  output [7:0] PeriphRead1,
  output [7:0] PeriphRead2,
  output [7:0] PeriphRead3,
  output [7:0] PeriphRead4,
  output [7:0] PeriphRead5,
  output [7:0] PeriphRead6,
  output [7:0] PeriphRead7,
  output [7:0] PeriphRead8
);

  wire demultiplexer_1_out0, demultiplexer_1_out1, demultiplexer_1_out2, demultiplexer_1_out3,
       demultiplexer_1_out4, demultiplexer_1_out5, demultiplexer_1_out6, demultiplexer_1_out7, Proc_outen;
  wire [7:0] multiplexer_1_out, Proc_addrperiph, Proc_dataout;

  cpu Proc (
    .clk(clk), .Reset(Reset), .DataIn(multiplexer_1_out), .AddrPeriph(Proc_addrperiph),
    .DataOut(Proc_dataout), .OutEn(Proc_outen));
  Demultiplexer #(.select(3), .enable("false")) demultiplexer_1 (
    .out0(demultiplexer_1_out0), .out1(demultiplexer_1_out1), .out2(demultiplexer_1_out2),
    .out3(demultiplexer_1_out3), .out4(demultiplexer_1_out4), .out5(demultiplexer_1_out5),
    .out6(demultiplexer_1_out6), .out7(demultiplexer_1_out7), .in(Proc_outen), .sel(Proc_addrperiph[2:0]));
  PeriphReg PeriphReg1 (
    .Clk(clk), .Reset(Reset), .DataCPU(Proc_dataout), .WECPU(demultiplexer_1_out0),
    .DataPeriph(PeriphWrite1), .WEPeriph(PeriphWE1), .PeriphOutput(PeriphRead1));
  PeriphReg PeriphReg2 (
    .Clk(clk), .Reset(Reset), .DataCPU(Proc_dataout), .WECPU(demultiplexer_1_out1),
    .DataPeriph(PeriphWrite2), .WEPeriph(PeriphWE2), .PeriphOutput(PeriphRead2));
  PeriphReg PeriphReg3 (
    .Clk(clk), .Reset(Reset), .DataCPU(Proc_dataout), .WECPU(demultiplexer_1_out2),
    .DataPeriph(PeriphWrite3), .WEPeriph(PeriphWE3), .PeriphOutput(PeriphRead3));
  PeriphReg PeriphReg4 (
    .Clk(clk), .Reset(Reset), .DataCPU(Proc_dataout), .WECPU(demultiplexer_1_out3),
    .DataPeriph(PeriphWrite4), .WEPeriph(PeriphWE4), .PeriphOutput(PeriphRead4));
  PeriphReg PeriphReg5 (
    .Clk(clk), .Reset(Reset), .DataCPU(Proc_dataout), .WECPU(demultiplexer_1_out4),
    .DataPeriph(PeriphWrite5), .WEPeriph(PeriphWE5), .PeriphOutput(PeriphRead5));
  PeriphReg PeriphReg6 (
    .Clk(clk), .Reset(Reset), .DataCPU(Proc_dataout), .WECPU(demultiplexer_1_out5),
    .DataPeriph(PeriphWrite6), .WEPeriph(PeriphWE6), .PeriphOutput(PeriphRead6));
  PeriphReg PeriphReg7 (
    .Clk(clk), .Reset(Reset), .DataCPU(Proc_dataout), .WECPU(demultiplexer_1_out6),
    .DataPeriph(PeriphWrite7), .WEPeriph(PeriphWE7), .PeriphOutput(PeriphRead7));
  PeriphReg PeriphReg8 (
    .Clk(clk), .Reset(Reset), .DataCPU(Proc_dataout), .WECPU(demultiplexer_1_out7),
    .DataPeriph(PeriphWrite8), .WEPeriph(PeriphWE8), .PeriphOutput(PeriphRead8));
  Multiplexer #(.select(3), .width(8), .enable("false")) multiplexer_1 (
    .in0(PeriphRead1), .in1(PeriphRead2), .in2(PeriphRead3), .in3(PeriphRead4), .in4(PeriphRead5),
    .in5(PeriphRead6), .in6(PeriphRead7), .in7(PeriphRead8), .out(multiplexer_1_out),
    .sel(Proc_addrperiph[2:0]));
endmodule

module PeriphReg (
  input  Clk,
  input  Reset,
  input  [7:0] DataCPU,
  input  WECPU,
  input  [7:0] DataPeriph,
  input  WEPeriph,
  output [7:0] PeriphOutput
);

  wire or_1_out;
  wire [7:0] multiplexer_1_out;

  Multiplexer #(.width(8), .enable("false")) multiplexer_1 (
    .in0(DataPeriph), .in1(DataCPU), .out(multiplexer_1_out), .sel(WECPU));
  or or_1 (or_1_out, WECPU, WEPeriph);
  Register register_1 (.D(multiplexer_1_out), .en(or_1_out), .clk(Clk), .Q(PeriphOutput), .clr(Reset));
endmodule
