// Logisim project compiled.circ as structural Verilog: 1 circuit, main circuit rom
module rom (
  input  [6:0] addr,
  output [15:0] data_out
);

  wire [15:0] mux0, mux1, mux2, mux3, undriven, undriven_2, undriven_3, undriven_4, undriven_5, undriven_6,
       undriven_7, undriven_8, undriven_9, undriven_10, undriven_11, undriven_12, undriven_13, undriven_14,
       undriven_15, undriven_16, undriven_17, undriven_18, undriven_19, undriven_20, undriven_21,
       undriven_22, undriven_23, undriven_24, undriven_25, undriven_26, undriven_27, undriven_28,
       undriven_29, undriven_30, undriven_31, undriven_32, undriven_33, undriven_34, undriven_35,
       undriven_36, undriven_37, undriven_38, undriven_39, undriven_40, undriven_41, undriven_42,
       undriven_43, undriven_44, undriven_45, undriven_46, undriven_47, undriven_48, undriven_49,
       undriven_50, undriven_51, undriven_52, undriven_53, undriven_54, undriven_55, undriven_56,
       undriven_57, undriven_58, undriven_59, undriven_60, undriven_61, undriven_62, undriven_63,
       undriven_64, undriven_65, undriven_66, undriven_67, undriven_68, undriven_69, undriven_70,
       undriven_71, undriven_72, undriven_73, undriven_74, undriven_75, undriven_76, undriven_77,
       undriven_78, undriven_79, undriven_80, undriven_81, undriven_82, undriven_83, undriven_84,
       undriven_85, undriven_86, undriven_87, undriven_88, undriven_89, undriven_90, undriven_91,
       undriven_92, undriven_93, undriven_94, undriven_95, undriven_96, undriven_97;

  Multiplexer #(.select(5), .width(16)) multiplexer_1 (
    .in0(16'h8a08), .in1(16'h8c01), .in2(16'hdc08), .in3(16'hc000), .in4(16'hc201), .in5(16'hc402),
    .in6(16'hd006), .in7(16'hd207), .in8(16'hd404), .in9(16'h68d8), .in10(16'hc603), .in11(16'h56e8),
    .in12(16'h6d20), .in13(16'ha8f4), .in14(16'h5d18), .in15(16'ha802), .in16(16'hbff1), .in17(16'h8c02),
    .in18(16'hdc08), .in19(16'hc000), .in20(16'hc402), .in21(16'hd005), .in22(16'hd404), .in23(16'h68d8),
    .in24(16'hc603), .in25(16'h56e8), .in26(16'h6d20), .in27(16'ha8f6), .in28(16'h5d18), .in29(16'ha8e4),
    .in30(16'hbff3), .in31(undriven_17), .out(mux0), .sel(addr[4:0]));  // open: en
  Multiplexer #(.select(5), .width(16)) multiplexer_2 (
    .in0(undriven), .in1(undriven_18), .in2(undriven_2), .in3(undriven_19), .in4(undriven_3),
    .in5(undriven_20), .in6(undriven_4), .in7(undriven_21), .in8(undriven_5), .in9(undriven_22),
    .in10(undriven_6), .in11(undriven_23), .in12(undriven_7), .in13(undriven_24), .in14(undriven_8),
    .in15(undriven_25), .in16(undriven_9), .in17(undriven_26), .in18(undriven_10), .in19(undriven_27),
    .in20(undriven_11), .in21(undriven_28), .in22(undriven_12), .in23(undriven_29), .in24(undriven_13),
    .in25(undriven_30), .in26(undriven_14), .in27(undriven_31), .in28(undriven_15), .in29(undriven_32),
    .in30(undriven_16), .in31(undriven_33), .out(mux1), .sel(addr[4:0]));  // open: en
  Multiplexer #(.select(5), .width(16)) multiplexer_3 (
    .in0(undriven_34), .in1(undriven_66), .in2(undriven_35), .in3(undriven_67), .in4(undriven_36),
    .in5(undriven_68), .in6(undriven_37), .in7(undriven_69), .in8(undriven_38), .in9(undriven_70),
    .in10(undriven_39), .in11(undriven_71), .in12(undriven_40), .in13(undriven_72), .in14(undriven_41),
    .in15(undriven_73), .in16(undriven_42), .in17(undriven_74), .in18(undriven_43), .in19(undriven_75),
    .in20(undriven_44), .in21(undriven_76), .in22(undriven_45), .in23(undriven_77), .in24(undriven_46),
    .in25(undriven_78), .in26(undriven_47), .in27(undriven_79), .in28(undriven_48), .in29(undriven_80),
    .in30(undriven_49), .in31(undriven_81), .out(mux2), .sel(addr[4:0]));  // open: en
  Multiplexer #(.select(5), .width(16)) multiplexer_4 (
    .in0(undriven_50), .in1(undriven_82), .in2(undriven_51), .in3(undriven_83), .in4(undriven_52),
    .in5(undriven_84), .in6(undriven_53), .in7(undriven_85), .in8(undriven_54), .in9(undriven_86),
    .in10(undriven_55), .in11(undriven_87), .in12(undriven_56), .in13(undriven_88), .in14(undriven_57),
    .in15(undriven_89), .in16(undriven_58), .in17(undriven_90), .in18(undriven_59), .in19(undriven_91),
    .in20(undriven_60), .in21(undriven_92), .in22(undriven_61), .in23(undriven_93), .in24(undriven_62),
    .in25(undriven_94), .in26(undriven_63), .in27(undriven_95), .in28(undriven_64), .in29(undriven_96),
    .in30(undriven_65), .in31(undriven_97), .out(mux3), .sel(addr[4:0]));  // open: en
  Multiplexer #(.select(2), .width(16)) multiplexer_5 (
    .in0(mux0), .in1(mux1), .in2(mux2), .in3(mux3), .out(data_out), .sel(addr[6:5]));  // open: en
  // Probe on data_out

  // Other names for the same wires on the sheet: sel[1:0] = addr[6:5]
endmodule
