// Logisim project sound_gen.circ as structural Verilog: 7 circuits, main circuit wave_gen
module wave_gen (
  input  clk,
  input  [15:0] phase_add,
  input  [7:0] waveform,
  output [15:0] sound
);

  wire [15:0] sawtooth_1_sound, sin_1_sound, square_1_sound, triangle_1_sound;
  wire [25:0] adder_1_out, bit_extender_1_out, phase_q;

  assign bit_extender_1_out = {{10{phase_add[15]}}, phase_add};  // Bit_Extender bit_extender_1
  Adder #(.width(26)) adder_1 (.a(bit_extender_1_out), .b(phase_q), .out(adder_1_out), .cin(1'b0));  // open: cout
  Register #(.width(26)) phase (.D(adder_1_out), .en(1'b1), .clk(clk), .Q(phase_q), .clr(1'b0));
  sin sin_1 (.phase(phase_q), .sound(sin_1_sound));
  square square_1 (.phase(phase_q), .sound(square_1_sound));
  sawtooth sawtooth_1 (.phase(phase_q), .sound(sawtooth_1_sound));
  triangle triangle_1 (.phase(phase_q), .sound(triangle_1_sound));
  Multiplexer #(.select(2), .width(16), .enable("false")) multiplexer_1 (
    .in0(sin_1_sound), .in1(square_1_sound), .in2(sawtooth_1_sound), .in3(triangle_1_sound), .out(sound),
    .sel(waveform[1:0]));
endmodule

module square (
  input  [25:0] phase,
  output [15:0] sound
);

  Multiplexer #(.width(16), .enable("false")) multiplexer_1 (
    .in0(16'h7fff), .in1(16'h8001), .out(sound), .sel(phase[25]));
endmodule

module sin (
  input  [25:0] phase,
  output [15:0] sound
);

  full_sin_lut full_sin_lut_1 (.addr(phase[25:15]), .data(sound));
endmodule

module amplitude (
  input  [15:0] sound_in,
  input  [15:0] amplitude,
  output [15:0] sound_amplified
);

  wire [14:0] multiplier_1_out;
  wire [15:0] adder_1_out;
  wire [15:15] multiplier_1_cout;

  Adder #(.width(16)) adder_1 (.a(sound_in), .b(16'h1), .out(adder_1_out));  // open: cin, cout
  Multiplier #(.width(16)) multiplier_1 (
    .a(adder_1_out), .b(amplitude), .out({sound_amplified[0], multiplier_1_out}),
    .cout({multiplier_1_cout[15], sound_amplified[15:1]}));  // open: cin
endmodule

module sawtooth (
  input  [25:0] phase,
  output [15:0] sound
);


  assign sound = phase[25:10];
endmodule

module triangle (
  input  [25:0] phase,
  output [15:0] sound
);

  wire [0:0] subtractor_1_out;
  wire [16:0] multiplexer_1_out, negator_1_out;

  Negator #(.width(17)) negator_1 (.in(phase[25:9]), .out(negator_1_out));
  Multiplexer #(.width(17), .enable("false")) multiplexer_1 (
    .in0(phase[25:9]), .in1(negator_1_out), .out(multiplexer_1_out), .sel(phase[25]));
  Subtractor #(.width(17)) subtractor_1 (
    .a(multiplexer_1_out), .b(17'h3fff), .out({sound, subtractor_1_out[0]}));  // open: bin, bout
endmodule

module sound_gen (
  input  clk,
  input  [15:0] phase_add,
  input  [7:0] waveform,
  input  [15:0] amplitude_in,
  output [15:0] sound
);

  wire [15:0] wave_gen_1_sound;

  wave_gen wave_gen_1 (.clk(clk), .phase_add(phase_add), .waveform(waveform), .sound(wave_gen_1_sound));
  amplitude amplitude_1 (.sound_in(wave_gen_1_sound), .amplitude(amplitude_in), .sound_amplified(sound));
endmodule
