// Logisim project theremin_toplevel.circ as structural Verilog: 2 circuits, main circuit theremin_toplevel
module theremin_toplevel (
  input  clk,
  input  PMOD_0_1,
  input  PMOD_1_1,
  input  [7:0] switches,
  input  [3:0] buttons,
  output PMOD_0_0,
  output PMOD_0_2,
  output PMOD_1_0,
  output PMOD_1_2,
  output [6:0] cathodes,
  output anode0,
  output anode1,
  output anode2,
  output anode3,
  output PMOD_2_0,
  output PMOD_2_1,
  output PMOD_2_2,
  output PMOD_2_3
);

  wire not_1_out, not_2_out, tlc548_1_cs, tlc548_1_io_clock, tlc548_2_cs, tlc548_2_io_clock;
  wire [7:0] bit_extender_1_out, CPU_Interface_1_p14, CPU_Interface_1_p15, CPU_Interface_1_p16,
       CPU_Interface_1_p17, dist_correct_1_data, dist_correct_2_data, soun_gen_ring_modulator_1_sound,
       soun_gen_ring_modulator_1_sound_2, tlc548_1_value, tlc548_2_value;
  wire [15:0] phase_add_correct_1_phase_add_out, phase_add_correct_2_phase_add_out;

  not not_1 (not_1_out, PMOD_0_1);
  not not_2 (not_2_out, PMOD_1_1);
  tlc548 tlc548_1 (
    .clk(clk), .data_in(not_1_out), .cs(tlc548_1_cs), .io_clock(tlc548_1_io_clock), .value(tlc548_1_value));
  not not_3 (PMOD_0_0, tlc548_1_cs);
  not not_4 (PMOD_0_2, tlc548_1_io_clock);
  tlc548 tlc548_2 (
    .clk(clk), .data_in(not_2_out), .cs(tlc548_2_cs), .io_clock(tlc548_2_io_clock), .value(tlc548_2_value));
  not not_5 (PMOD_1_0, tlc548_2_cs);
  not not_6 (PMOD_1_2, tlc548_2_io_clock);
  assign bit_extender_1_out = {{4{buttons[3]}}, buttons};  // Bit_Extender bit_extender_1
  dist_correct dist_correct_1 (.addr(tlc548_1_value), .data(dist_correct_1_data));
  dist_correct dist_correct_2 (.addr(tlc548_2_value), .data(dist_correct_2_data));
  // CPU_Interface CPU_Interface_1: pin names not known; wires that end beside it: clk, dist_correct_1_data, 1'b1, dist_correct_2_data, 1'b1, switches, 1'b1, bit_extender_1_out, 1'b1, 1'b0, 1'b0, 1'b0, 1'b0, CPU_Interface_1_p14, CPU_Interface_1_p15, CPU_Interface_1_p16, CPU_Interface_1_p17
  phase_add_correct phase_add_correct_1 (
    .phase_add_in(CPU_Interface_1_p16), .min(16'h85), .shift(4'b0010),
    .phase_add_out(phase_add_correct_1_phase_add_out));
  phase_add_correct phase_add_correct_2 (
    .phase_add_in(CPU_Interface_1_p15), .min(16'h85), .shift(4'b0010),
    .phase_add_out(phase_add_correct_2_phase_add_out));
  soun_gen_ring_modulator soun_gen_ring_modulator_1 (
    .clk(clk), .phase_add(phase_add_correct_1_phase_add_out), .waveform(CPU_Interface_1_p14),
    .amplitude_in({1'b0, CPU_Interface_1_p17, {7{1'b0}}}),
    .phase_add_ring(phase_add_correct_2_phase_add_out),
    .sound({soun_gen_ring_modulator_1_sound_2, soun_gen_ring_modulator_1_sound}));
  bytes_display bytes_debug (
    .octet1(soun_gen_ring_modulator_1_sound_2), .octet1_enable(1'b1),
    .octet2(soun_gen_ring_modulator_1_sound), .octet2_enable(1'b1), .reset(1'b0), .clk(clk),
    .cathodes(cathodes), .anode0(anode0), .anode1(anode1), .anode2(anode2), .anode3(anode3));
  cs4344_mono cs4344_mono_1 (
    .clk(clk), .rst(1'b0), .audio_in({soun_gen_ring_modulator_1_sound_2, soun_gen_ring_modulator_1_sound}),
    .SDOUT(PMOD_2_3), .SCLK(PMOD_2_2), .MCLK(PMOD_2_0), .LRCK(PMOD_2_1));  // open: done
endmodule

module phase_add_correct (
  input  [7:0] phase_add_in,
  input  [15:0] min,
  input  [3:0] shift,
  output [15:0] phase_add_out
);

  wire [15:0] bit_extender_1_out, shifter_1_out;

  assign bit_extender_1_out = {{8{phase_add_in[7]}}, phase_add_in};  // Bit_Extender bit_extender_1
  Shifter #(.width(16)) shifter_1 (.in(bit_extender_1_out), .\dist (shift), .out(shifter_1_out));
  Adder #(.width(16)) adder_1 (.a(min), .b(shifter_1_out), .out(phase_add_out));  // open: cin, cout
endmodule
